// Logisim project nandy.circ as structural Verilog: 10 circuits, main circuit CPU
module CPU (
  input  Int,
  input  Reset,
  input  Clock,
  input  [7:0] Input,
  output [7:0] Output,
  output IOWrite,
  output IORead
);

  wire alu_1_carry, and_1_out, Carry_q, control_1_cli, control_1_isp, control_1_j, control_1_lj,
       control_1_ljr, control_1_m, control_1_mc, control_1_mw, control_1_rd, control_1_s, control_1_wa,
       control_1_wc, control_1_wr, control_1_y, d_ff_1_q, intctrl_1_ie_2, intctrl_1_is_2, Last_q, not_1_out,
       not_2_out, not_3_out, not_4_out;
  wire [1:0] control_1_rs;
  wire [3:0] control_1_alu, IL_q, IL_q_2;
  wire [7:0] alu_1_q, control_1_signal, mem_1_dout, regfile_1_acc, regfile_1_dx, regfile_1_dy,
       regfile_1_outa, regfile_1_outb, regfile_1_sp;
  wire [15:0] addrcalc_1_addr, addrcalc_1_pc_2, addrcalc_1_ret, intctrl_1_pcout, PC_q;

  not not_1 (not_1_out, Last_q);
  Register #(.width(1)) Last (.D(Int), .en(not_2_out), .Q(Last_q), .clk(Clock));  // open: clr
  not not_2 (not_2_out, control_1_mc);
  and and_1 (and_1_out, Int, not_1_out);
  Control control_1 (
    .M(control_1_m), .S(control_1_s), .J(control_1_j), .LJ(control_1_lj), .MW(control_1_mw),
    .MC(control_1_mc), .RD(control_1_rd), .WR(control_1_wr), .Y(control_1_y), .RS(control_1_rs),
    .WA(control_1_wa), .ISP(control_1_isp), .LJR(control_1_ljr), .WC(control_1_wc), .Inst({IL_q_2, IL_q}),
    .Cycle(d_ff_1_q), .Carry(Carry_q), .ALU(control_1_alu), .Signal(control_1_signal), .CLI(control_1_cli));
  not not_3 (not_3_out, control_1_m);
  IntCtrl intctrl_1 (
    .PCin(addrcalc_1_pc_2), .IE(control_1_signal[5]), .ID(control_1_signal[4]), .INT(and_1_out),
    ._2C(control_1_mc), .CLR(control_1_cli), .CLK(Clock), .PCout(intctrl_1_pcout), .IS_2(intctrl_1_is_2),
    .IE_2(intctrl_1_ie_2), .RST(Reset), .IS(control_1_signal[7]), .IC(control_1_signal[6]));
  Register #(.width(16)) PC (.D(intctrl_1_pcout), .en(not_3_out), .Q(PC_q), .clk(Clock), .clr(Reset));
  RegFile regfile_1 (
    .Return(addrcalc_1_ret), .CLK(Clock), .Input(alu_1_q), .RD(control_1_rd), .WA(control_1_wa),
    .IOin(Input), .Y(control_1_y), .ISP(control_1_isp), ._2C(d_ff_1_q), .LJR(control_1_ljr),
    .INT(intctrl_1_is_2), .WR(control_1_wr), .Mem(mem_1_dout), .Imm(IL_q), .RS(control_1_rs),
    .IA(addrcalc_1_pc_2), .ACC(regfile_1_acc), .SP(regfile_1_sp), .DX(regfile_1_dx), .DY(regfile_1_dy),
    .OutA(regfile_1_outa), .OutB(regfile_1_outb), .IO(Output), .OnWrite(IOWrite), .OnRead(IORead),
    .IE(intctrl_1_ie_2));
  AddrCalc addrcalc_1 (
    .PC(PC_q), .DX(regfile_1_dx), .DY(regfile_1_dy), .SP(regfile_1_sp), .Stack(control_1_s),
    .LongOffs(mem_1_dout), .Offs(IL_q), .Mem(control_1_m), .Jump(control_1_j), .Addr(addrcalc_1_addr),
    .LongJump(control_1_lj), .PC_2(addrcalc_1_pc_2), .Ret(addrcalc_1_ret));
  Mem mem_1 (.ADDR(addrcalc_1_addr), .DIN(regfile_1_acc), .WE(control_1_mw), .CLK(Clock), .DOUT(mem_1_dout));
  Register #(.width(1)) Carry (.D(alu_1_carry), .en(control_1_wc), .Q(Carry_q), .clk(Clock));  // open: clr
  ALU alu_1 (
    .A(regfile_1_outa), .B(regfile_1_outb), .ALUop(control_1_alu), .Carry(alu_1_carry), .Q(alu_1_q),
    .CarryIn(Carry_q), .XY(control_1_y));
  D_Flip_Flop d_ff_1 (.clk(Clock), .D(control_1_mc), .Q(d_ff_1_q));  // open: Qn, preset, en, reset
  Register #(.trigger("high")) IL (.D(mem_1_dout), .Q({IL_q_2, IL_q}), .clk(not_4_out));  // open: en, clr
  not not_4 (not_4_out, d_ff_1_q);
endmodule

module ALU (
  input  [7:0] A,
  input  [7:0] B,
  input  [3:0] ALUop,
  input  CarryIn,
  input  XY,
  output [7:0] Q,
  output Carry
);

  wire comparator_1_eq, multiplexer_1_out, multiplexer_4_out, odd_parity_1_out;
  wire [0:0] multiplexer_2_out;
  wire [7:0] adder_1_out, and_1_out, bit_extender_1_out, bit_extender_2_out, multiplexer_3_out, or_1_out,
       xor_1_out, xor_2_out, xor_4_out;
  wire [8:0] multiplexer_5_out, multiplexer_6_out, multiplexer_7_out;
  wire [8:8] adder_1_cout, xor_3_out;

  assign or_1_out = A | B;  // OR_Gate or_1, 8 bits wide
  assign and_1_out = A & B;  // AND_Gate and_1, 8 bits wide
  assign xor_1_out = A ^ B;  // XOR_Gate xor_1, 8 bits wide
  assign xor_2_out = B ^ bit_extender_1_out;  // XOR_Gate xor_2, 8 bits wide
  assign bit_extender_1_out = {{7{ALUop[1]}}, ALUop[1]};  // Bit_Extender bit_extender_1
  Multiplexer #(.enable("false")) multiplexer_1 (
    .in0(ALUop[1]), .in1(CarryIn), .out(multiplexer_1_out), .sel(ALUop[0]));
  Adder adder_1 (.a(A), .b(xor_2_out), .out(adder_1_out), .cin(multiplexer_1_out), .cout(adder_1_cout[8]));
  Multiplexer #(.select(2), .enable("false")) multiplexer_2 (
    .in0(1'b0), .in1(CarryIn), .in2(A[0]), .in3(A[7]), .out(multiplexer_2_out[0]), .sel(ALUop[1:0]));
  xor odd_parity_1 (odd_parity_1_out, A[0], A[1], A[2], A[3], A[4], A[5], A[6], A[7]);
  Comparator comparator_1 (.a(A), .b({8{1'b0}}), .eq(comparator_1_eq));  // open: gt, lt
  Multiplexer #(.select(2), .width(8), .enable("false")) multiplexer_3 (
    .in0(B), .in1(or_1_out), .in2(and_1_out), .in3(xor_1_out), .out(multiplexer_3_out), .sel(ALUop[1:0]));
  Multiplexer #(.select(2), .enable("false")) multiplexer_4 (
    .in0(A[7]), .in1(CarryIn), .in2(comparator_1_eq), .in3(odd_parity_1_out), .out(multiplexer_4_out),
    .sel(ALUop[1:0]));
  assign bit_extender_2_out = {{7{ALUop[2]}}, ALUop[2]};  // Bit_Extender bit_extender_2
  xor xor_3 (xor_3_out[8], multiplexer_4_out, ALUop[2]);
  assign xor_4_out = multiplexer_3_out ^ bit_extender_2_out;  // XOR_Gate xor_4, 8 bits wide
  Multiplexer #(.width(9), .enable("false")) multiplexer_5 (
    .in0({A, multiplexer_2_out[0]}), .in1({A[0], multiplexer_2_out[0], A[7:1]}), .out(multiplexer_5_out),
    .sel(XY));
  Multiplexer #(.width(9), .enable("false")) multiplexer_6 (
    .in0({xor_3_out[8], xor_4_out}), .out(multiplexer_6_out), .sel(ALUop[2]));  // open: in1
  Multiplexer #(.width(9), .enable("false")) multiplexer_7 (
    .in0({adder_1_cout[8], adder_1_out}), .in1(multiplexer_5_out), .out(multiplexer_7_out), .sel(ALUop[2]));
  Multiplexer #(.width(9), .enable("false")) multiplexer_8 (
    .in0(multiplexer_6_out), .in1(multiplexer_7_out), .out({Carry, Q}), .sel(ALUop[3]));
endmodule

module Mem (
  input  [15:0] ADDR,
  input  [7:0] DIN,
  input  WE,
  input  CLK,
  output [7:0] DOUT
);

  wire [7:0] ram_1_data, rom_1_data;

  ROM #(.addrWidth(15)) rom_1 (.addr(ADDR[14:0]), .data(rom_1_data));  // open: sel
  RAM #(.addrWidth(15), .bus("separate")) ram_1 (
    .addr(ADDR[14:0]), .din(DIN), .data(ram_1_data), .str(WE), .sel(1'b1), .clk(CLK), .ld(1'b1), .clr(1'b0));
  Multiplexer #(.width(8), .enable("false")) multiplexer_1 (
    .in0(rom_1_data), .in1(ram_1_data), .out(DOUT), .sel(ADDR[15]));

  // Notes on the sheet:
  //   contents of rom_1 (hex, n*v repeats v):
  //   c0 0 8 1d b c0 4 a c0 0 f 10 32500*0 2d b2 e b0 7 b1 6 c0 0 a b 90 a 91 b 92 23 12 ff
endmodule

module AddrCalc (
  input  [15:0] PC,
  input  [7:0] DX,
  input  [7:0] DY,
  input  [7:0] SP,
  input  [7:0] LongOffs,
  input  [3:0] Offs,
  input  Mem,
  input  Stack,
  input  Jump,
  input  LongJump,
  output [15:0] Addr,
  output [15:0] Ret,
  output [15:0] PC_2
);

  wire [15:0] bit_extender_1_out, bit_extender_2_out, multiplexer_1_out, multiplexer_2_out,
       multiplexer_3_out, multiplexer_4_out;

  Multiplexer #(.width(16), .enable("false")) multiplexer_1 (
    .in0({DY, DX}), .in1({{8{1'b1}}, SP}), .out(multiplexer_1_out), .sel(Stack));
  assign bit_extender_1_out = {{4{Offs[3]}}, {Offs, LongOffs}};  // Bit_Extender bit_extender_1
  assign bit_extender_2_out = {{12{1'b0}}, Offs};  // Bit_Extender bit_extender_2
  Multiplexer #(.width(16), .enable("false")) multiplexer_2 (
    .in0(PC), .in1(multiplexer_1_out), .out(multiplexer_2_out), .sel(Mem));
  Multiplexer #(.width(16), .enable("false")) multiplexer_3 (
    .in0(16'h1), .in1(bit_extender_1_out), .out(multiplexer_3_out), .sel(Jump));
  Adder #(.width(16)) adder_1 (.a(multiplexer_2_out), .b(multiplexer_4_out), .out(Ret), .cin(1'b0));  // open: cout
  Multiplexer #(.width(16), .enable("false")) multiplexer_4 (
    .in0(multiplexer_3_out), .in1(bit_extender_2_out), .out(multiplexer_4_out), .sel(Mem));
  Multiplexer #(.width(16), .enable("false")) multiplexer_5 (.in0(PC), .in1(Ret), .out(Addr), .sel(Mem));
  Multiplexer #(.width(16), .enable("false")) multiplexer_6 (.in0(Ret), .in1({DY, DX}), .out(PC_2), .sel(LongJump));
endmodule

module RegFile (
  input  [15:0] Return,
  input  CLK,
  input  [7:0] Input,
  input  RD,
  input  WA,
  input  [7:0] IOin,
  input  Y,
  input  ISP,
  input  _2C,
  input  LJR,
  input  WR,
  input  [7:0] Mem,
  input  [3:0] Imm,
  input  [1:0] RS,
  input  [15:0] IA,
  input  INT,
  input  IE,
  output [7:0] ACC,
  output [7:0] SP,
  output [7:0] DX,
  output [7:0] DY,
  output OnRead,
  output [7:0] OutA,
  output [7:0] OutB,
  output [7:0] IO,
  output OnWrite
);

  wire and_1_out, and_2_out, and_3_out, and_4_out, and_5_out, and_7_out, decoder_1_out0, decoder_1_out1,
       decoder_1_out2, decoder_1_out3, demultiplexer_1_out0, demultiplexer_1_out1, demultiplexer_2_out0,
       demultiplexer_2_out1, not_1_out, or_1_out, or_2_out, or_3_out, or_4_out, or_5_out, or_6_out;
  wire [7:0] bit_extender_1_out, DX_q, DY_q, IRX_q, IRY_q, multiplexer_1_out, multiplexer_2_out,
       multiplexer_3_out, multiplexer_4_out, multiplexer_5_out, multiplexer_6_out, multiplexer_9_out,
       multiplexer_10_out, multiplexer_11_out, multiplexer_12_out, multiplexer_13_out;

  assign bit_extender_1_out = {{4{Imm[3]}}, Imm};  // Bit_Extender bit_extender_1
  Decoder #(.select(2), .enable("false")) decoder_1 (
    .out0(decoder_1_out0), .out1(decoder_1_out1), .out2(decoder_1_out2), .out3(decoder_1_out3), .sel(RS));
  and and_1 (and_1_out, decoder_1_out1, RD);
  and and_2 (and_2_out, decoder_1_out0, WR);
  and and_3 (and_3_out, decoder_1_out2, WR);
  and and_4 (and_4_out, decoder_1_out3, WR);
  and and_5 (and_5_out, WR, decoder_1_out1);
  and and_6 (OnRead, CLK, and_1_out);
  or or_1 (or_1_out, RD, WA);
  or or_2 (or_2_out, and_2_out, ISP);
  or or_3 (or_3_out, and_3_out, LJR);
  or or_4 (or_4_out, and_4_out, LJR);
  not not_1 (not_1_out, INT);
  Multiplexer #(.width(8), .enable("false")) multiplexer_1 (
    .in0(Input), .in1(multiplexer_10_out), .out(multiplexer_1_out), .sel(RD));
  Multiplexer #(.width(8), .enable("false")) multiplexer_2 (.in0(Input), .in1(ACC), .out(multiplexer_2_out), .sel(WR));
  Multiplexer #(.width(8), .enable("false")) multiplexer_3 (
    .in0(Return[7:0]), .in1(ACC), .out(multiplexer_3_out), .sel(WR));
  Multiplexer #(.width(8), .enable("false")) multiplexer_4 (
    .in0(Return[15:8]), .in1(ACC), .out(multiplexer_4_out), .sel(WR));
  Multiplexer #(.width(8), .enable("false")) multiplexer_5 (
    .in0(multiplexer_3_out), .in1(IA[7:0]), .out(multiplexer_5_out), .sel(not_1_out));
  Multiplexer #(.width(8), .enable("false")) multiplexer_6 (
    .in0(multiplexer_4_out), .in1(IA[15:8]), .out(multiplexer_6_out), .sel(not_1_out));
  Demultiplexer #(.enable("false")) demultiplexer_1 (
    .out0(demultiplexer_1_out0), .out1(demultiplexer_1_out1), .in(or_3_out), .sel(INT));
  Demultiplexer #(.enable("false")) demultiplexer_2 (
    .out0(demultiplexer_2_out0), .out1(demultiplexer_2_out1), .in(or_4_out), .sel(INT));
  or or_5 (or_5_out, demultiplexer_1_out1, and_7_out);
  or or_6 (or_6_out, demultiplexer_2_out1, and_7_out);
  and and_7 (and_7_out, not_1_out, IE);
  Register u_ACC (.D(multiplexer_1_out), .en(or_1_out), .Q(ACC), .clk(CLK));  // open: clr
  Register u_SP (.D(multiplexer_2_out), .en(or_2_out), .Q(SP), .clk(CLK));  // open: clr
  Register u_DX (.D(multiplexer_3_out), .en(demultiplexer_1_out0), .Q(DX_q), .clk(CLK));  // open: clr
  Register u_DY (.D(multiplexer_4_out), .en(demultiplexer_2_out0), .Q(DY_q), .clk(CLK));  // open: clr
  Register IRX (.D(multiplexer_5_out), .en(or_5_out), .Q(IRX_q), .clk(CLK));  // open: clr
  Register IRY (.D(multiplexer_6_out), .en(or_6_out), .Q(IRY_q), .clk(CLK));  // open: clr
  Register u_IO (.D(ACC), .en(and_5_out), .Q(IO), .clk(CLK));  // open: clr
  Multiplexer #(.width(8), .enable("false")) multiplexer_7 (.in0(DX_q), .in1(IRX_q), .out(DX), .sel(INT));
  Multiplexer #(.width(8), .enable("false")) multiplexer_8 (.in0(DY_q), .in1(IRY_q), .out(DY), .sel(INT));
  and and_8 (OnWrite, CLK, and_5_out);
  Multiplexer #(.width(8), .enable("false")) multiplexer_9 (.in0(DX), .in1(IOin), .out(multiplexer_9_out), .sel(RS[0]));
  Multiplexer #(.width(8), .enable("false")) multiplexer_10 (
    .in0(multiplexer_9_out), .in1(multiplexer_11_out), .out(multiplexer_10_out), .sel(RS[1]));
  Multiplexer #(.width(8), .enable("false")) multiplexer_11 (.in0(DX), .in1(DY), .out(multiplexer_11_out), .sel(RS[0]));
  Multiplexer #(.width(8), .enable("false")) multiplexer_12 (.in0(DX), .in1(DY), .out(multiplexer_12_out), .sel(Y));
  Multiplexer #(.width(8), .enable("false")) multiplexer_13 (
    .in0(multiplexer_12_out), .in1(Mem), .out(multiplexer_13_out), .sel(_2C));
  Multiplexer #(.width(8), .enable("false")) multiplexer_14 (.in0(ACC), .in1(SP), .out(OutA), .sel(ISP));
  Multiplexer #(.width(8), .enable("false")) multiplexer_15 (
    .in0(multiplexer_13_out), .in1(bit_extender_1_out), .out(OutB), .sel(ISP));
endmodule

module Control (
  input  [7:0] Inst,
  input  Cycle,
  input  Carry,
  output M,
  output S,
  output J,
  output LJ,
  output CLI,
  output LJR,
  output MW,
  output MC,
  output RD,
  output WR,
  output Y,
  output [1:0] RS,
  output WA,
  output ISP,
  output WC,
  output [3:0] ALU,
  output [7:0] Signal
);

  wire and_2_out, and_5_out, and_6_out, and_7_out, and_8_out, and_10_out, and_16_out, and_17_out, nand_1_out,
       not_1_out, not_2_out, not_3_out, not_4_out, not_5_out, not_6_out, not_7_out, not_8_out, not_9_out,
       not_10_out, not_11_out, not_12_out, not_13_out, not_14_out, not_15_out, not_16_out, not_18_out,
       not_19_out, not_20_out, not_21_out, not_22_out, or_1_out, or_2_out;
  wire [1:1] not_17_out;

  not not_1 (not_1_out, Inst[6]);
  not not_2 (not_2_out, Inst[7]);
  not not_3 (not_3_out, Inst[6]);
  not not_4 (not_4_out, Inst[5]);
  not not_5 (not_5_out, Inst[3]);
  not not_6 (not_6_out, Cycle);
  not not_7 (not_7_out, Inst[7]);
  not not_8 (not_8_out, Inst[6]);
  not not_9 (not_9_out, Inst[5]);
  not not_10 (not_10_out, Inst[4]);
  not not_11 (not_11_out, Inst[7]);
  not not_12 (not_12_out, Inst[5]);
  not not_13 (not_13_out, Inst[3]);
  not not_14 (not_14_out, Inst[2]);
  not not_15 (not_15_out, Inst[7]);
  not not_16 (not_16_out, Inst[6]);
  not not_17 (not_17_out[1], Inst[7]);
  not not_18 (not_18_out, Inst[5]);
  not not_19 (not_19_out, Inst[6]);
  not not_20 (not_20_out, Inst[7]);
  and and_1 (M, Inst[7], Cycle, not_1_out);
  and and_2 (and_2_out, Inst[7], Inst[6], Inst[5], Cycle);
  and and_3 (LJ, not_2_out, not_3_out, not_4_out, Inst[4], not_5_out);
  and and_4 (MC, not_6_out, Inst[7]);
  and and_5 (and_5_out, not_7_out, not_8_out, not_9_out, not_10_out);
  and and_6 (and_6_out, not_11_out, Inst[6]);
  and and_7 (and_7_out, Inst[7], Cycle, Inst[6], not_12_out);
  and and_8 (and_8_out, Inst[4], not_13_out, not_14_out);
  and and_9 (ISP, not_15_out, not_16_out, Inst[5]);
  Decoder #(.select(3), .disabled(0)) decoder_1 (
    .out0(Signal[0]), .out1(Signal[1]), .out2(Signal[2]), .out3(Signal[3]), .out4(Signal[4]),
    .out5(Signal[5]), .out6(Signal[6]), .out7(Signal[7]), .sel(Inst[2:0]), .en(and_10_out));
  and and_10 (and_10_out, not_18_out, not_19_out, not_20_out, Inst[3], Inst[4]);
  nand nand_1 (nand_1_out, Carry, Inst[4]);
  and and_11 (CLI, LJ, Inst[1]);
  and and_12 (LJR, LJ, Inst[2]);
  and and_13 (MW, M, Inst[5]);
  and and_14 (RD, Inst[2], and_5_out);
  and and_15 (WR, and_5_out, Inst[3]);
  or or_1 (or_1_out, and_6_out, and_7_out);
  and and_16 (and_16_out, M, not_22_out);
  and and_17 (and_17_out, or_1_out, not_21_out);
  not not_21 (not_21_out, and_8_out);
  or or_2 (or_2_out, or_1_out, ISP);
  Multiplexer #(.width(4), .enable("false")) multiplexer_1 (
    .in0({2'b00, not_17_out[1], 1'b0}), .in1(Inst[3:0]), .out(ALU), .sel(Inst[6]));
  and and_18 (J, and_2_out, nand_1_out);
  not not_22 (not_22_out, MW);
  or or_3 (WA, and_16_out, and_17_out);
  and and_19 (WC, or_2_out, Inst[4]);

  assign RS = Inst[1:0];
  assign S = Inst[4];
  assign Y = Inst[5];
endmodule

module IntCtrl (
  input  [15:0] PCin,
  input  IE,
  input  ID,
  input  INT,
  input  _2C,
  input  CLR,
  input  CLK,
  input  RST,
  input  IS,
  input  IC,
  output [15:0] PCout,
  output IE_2,
  output IS_2
);

  wire and_1_out, not_1_out, not_2_out, or_1_out, or_2_out;

  not not_1 (not_1_out, _2C);
  not not_2 (not_2_out, IS_2);
  Multiplexer #(.width(16), .enable("false")) multiplexer_1 (.in0(PCin), .in1(16'h7f00), .out(PCout), .sel(and_1_out));
  and and_1 (and_1_out, IE_2, INT, not_1_out, not_2_out);
  or or_1 (or_1_out, and_1_out, IS);
  or or_2 (or_2_out, CLR, IC);
  S_R_Flip_Flop s_r_ff_1 (.S(IE), .clk(CLK), .R(ID), .Q(IE_2), .reset(RST));  // open: Qn, preset, en
  S_R_Flip_Flop s_r_ff_2 (.S(or_1_out), .clk(CLK), .R(or_2_out), .Q(IS_2), .reset(RST));  // open: Qn, preset, en
endmodule

module test (
  input  A,
  input  B,
  input  XOR,
  output Q,
  output Q_2
);

  wire nand_1_out, nand_2_out, nand_3_out, nand_4_out, nand_5_out, nand_6_out, nand_7_out, nand_8_out;

  nand nand_1 (nand_1_out, A, B);
  nand nand_2 (nand_2_out, nand_1_out, nand_1_out);
  nand nand_3 (nand_3_out, A, nand_4_out);
  nand nand_4 (nand_4_out, A, XOR, B);
  nand nand_5 (nand_5_out, nand_4_out, B);
  nand nand_6 (nand_6_out, A, nand_7_out);
  nand nand_7 (nand_7_out, XOR, nand_2_out);
  nand nand_8 (nand_8_out, nand_7_out, B);
  nand nand_9 (Q, nand_3_out, nand_5_out);
  nand nand_10 (Q_2, nand_6_out, nand_8_out);
endmodule

module test2 (
  input  Op1,
  input  Op0,
  input  A,
  input  B,
  output Q
);

  wire nand_1_out, nand_2_out, nand_3_out, nand_4_out, nand_5_out, nand_6_out, nand_7_out, nand_8_out,
       nand_9_out, nand_10_out;

  nand nand_1 (nand_1_out, Op1, Op1);
  nand nand_2 (nand_2_out, Op0, Op0);
  nand nand_3 (nand_3_out, A, Op1, B);
  nand nand_4 (nand_4_out, nand_1_out, B);
  nand nand_5 (nand_5_out, A, nand_3_out);
  nand nand_6 (nand_6_out, nand_3_out, B);
  nand nand_7 (nand_7_out, nand_4_out, nand_3_out);
  nand nand_8 (nand_8_out, nand_7_out, nand_2_out);
  nand nand_9 (nand_9_out, Op0, nand_10_out);
  nand nand_10 (nand_10_out, nand_5_out, nand_6_out);
  nand nand_11 (Q, nand_8_out, nand_9_out);
endmodule

module ram (
  input  [14:0] ADDR,
  input  WR,
  input  [7:0] DIN,
  output [7:0] DOUT
);

  wire nand_1_out;
  wire [7:0] bit_extender_1_out, pull_resistor_1_node;

  nand nand_1 (nand_1_out, WR, WR);
  Pull_Resistor #(.pull(1)) pull_resistor_1 (.node(pull_resistor_1_node));
  RAM #(.addrWidth(15), .bus("asynch")) ram_1 (
    .addr(ADDR), .data(pull_resistor_1_node), .sel(1'b1), .ld(nand_1_out), .clr(1'b0));
  assign bit_extender_1_out = {{7{WR}}, WR};  // Bit_Extender bit_extender_1
  assign pull_resistor_1_node = ~(bit_extender_1_out & DIN);  // NAND_Gate nand_2, 8 bits wide
  assign DOUT = ~(pull_resistor_1_node & pull_resistor_1_node);  // NAND_Gate nand_3, 8 bits wide

  // Notes on the sheet:
  //   nand_2 drives only 0 and floats otherwise
endmodule
